# Fritzing sketch wiring-diagram (saved by Fritzing 0.9.5d)

parts:
  Mod1 = Nano-V3-0-IO-Expansion-Adapter
  Composant1 = Arduino Nano (Rev3.0)
  LED1 = smd LED [color="Red (633nm)" package="0805 [SMD]"]
  LED2 = smd LED [color="Green (555nm)" package="0805 [SMD]"]
  SG2 = Buzzer 12mm [package=buzzer-12mm-ns]
  ENC28J1 = ENC28J60

nets:
  N1: Mod1.RST, Composant1.RESET
  VIN: Mod1.VIN, Composant1.VIN
  N2: Mod1.A0, Composant1.A0
  N3: Mod1.A1, Composant1.A1
  N4: Mod1.A2, Composant1.A2
  N5: Mod1.A3, Composant1.A3
  N6: Mod1.A5/SCL, Composant1.A5, ENC28J1.5v
  N7: Mod1.A6, Composant1.A6
  N8: Mod1.A7, Composant1.A7
  N9: Mod1.D13/SCK, Composant1.D13/SCK
  N10: Mod1.NC, Composant1.3V3
  N11: Mod1.AREF, Composant1.AREF
  N12: Mod1.A4/SDA, Composant1.A4, ENC28J1.GND
  VCC: Mod1.VCC, Composant1.5V
  GND: Mod1.GND, Composant1.GND, LED1.cathode, LED2.cathode, SG2.2
  N13: Mod1.D12/MISO, Composant1.D12/MISO
  N14: Mod1.D11_PWM/MOSI, Composant1.D11/MOSI
  N15: Mod1.D10_PWM/SS, Composant1.D10
  N16: Mod1.D9_PWM, Composant1.D9
  N17: Mod1.D8, Composant1.D8
  N18: Mod1.D7, Composant1.D7
  N19: Mod1.D6_PWM, Composant1.D6, SG2.1
  N20: Mod1.D5_PWM, Composant1.D5, LED1.anode
  N21: Mod1.D4, Composant1.D4, LED2.anode
  N22: Mod1.D3_PWM, Composant1.D3
  N23: Mod1.D2, Composant1.D2
  N24: Mod1.D0/RX#64, Mod1.D1/TX#129, Composant1.D0/RX
  N25: Mod1.D1/TX#65, Mod1.D0/RX#128, Composant1.D1/TX

custom parts:
  Nano-V3-0-IO-Expansion-Adapter: Nano V3.0 IO Expansion Adapter Shield. Note pcb view has been supressed as not useful. You can drag a Nano over the Nano connectors and it will connect and appear in schematic (although at present due to a bug, routing will not show as complete in breadboard).
  ENC28J60: Ethernet Module ENC28J60
